# Fritzing sketch project (saved by Fritzing 0.9.3b)
circuit board: 8.46667cm x 6.44cm
perfboards: 1

parts:
  U1 = NodeMCU V1.0
  IC1 = IC, DIP package, 16 pins [chip_label=CD4051]
  Port1 = female pin header, 3 pins [form="♀ (female)"]
  Port3 = female pin header, 3 pins [form="♀ (female)"]
  Port4 = female pin header, 3 pins [form="♀ (female)"]
  Port2 = female pin header, 3 pins [form="♀ (female)"]
  Port5 = female pin header, 3 pins [form="♀ (female)"]
  Port6 = female pin header, 3 pins [form="♀ (female)"]
  Port7 = female pin header, 3 pins [form="♀ (female)"]
  Port8 = female pin header, 3 pins [form="♀ (female)"]
  Port10 = female pin header, 3 pins [form="♀ (female)"]
  R1 = Resistor [tolerance=±5% resistance=10k package="0805 [SMD]"]

nets:
  N1: U1.D1, Port10.pin2, R1.Pin_0
  N2: U1.3V3, IC1.pin16, Port1.pin2, Port3.pin2, Port4.pin2, Port2.pin2, Port5.pin2, Port6.pin2, Port7.pin2, Port8.pin2, Port10.pin1
  N3: U1.GND, IC1.pin6, IC1.pin7, IC1.pin8, Port1.pin3, Port3.pin3, Port4.pin3, Port2.pin3, Port5.pin3, Port6.pin3, Port7.pin3, Port8.pin3
  N4: U1.D6, IC1.pin9
  N5: U1.D7, IC1.pin10
  N6: U1.D8, IC1.pin11
  N7: U1.A0, IC1.pin3
  N8: IC1.pin1, Port4.pin1
  N9: IC1.pin2, Port3.pin1
  N10: IC1.pin4, Port2.pin1
  N11: IC1.pin5, Port1.pin1
  N12: IC1.pin12, Port8.pin1
  N13: IC1.pin13, Port7.pin1
  N14: IC1.pin14, Port6.pin1
  N15: IC1.pin15, Port5.pin1

custom parts:
  NodeMCU V1.0: ESP8266 based NodeMCU
